# Fritzing sketch 2022-02-03-lidar-uno-and-servos (saved by Fritzing 0.9.3b)
stripboards: 1

parts:
  Arduino_Uno = Arduino Uno (Rev3) - ICSP
  C1 = Electrolytic Capacitor [capacitance=1000µF package="300 mil [THT, electrolytic]"]
  Lidar_LIte_V3 = Header 6 [package=1x06_smd_straight_combo]
  Screw_terminal = Header 4 [package=screwterminal-3.5mm-4_lock]
  R1 = Resistor [tolerance=±5% resistance=4.7k package="2010 [SMD]"]
  R2 = Resistor [tolerance=±5% resistance=4.7k package="2010 [SMD]"]
  J1 = Basic Servo
  J2 = Basic Servo
  JP1 = Header 3 [package=screwterminal-3.5mm-3_lock.007s]
  JP2 = Header 3 [package=screwterminal-3.5mm-3_lock.007s]

nets:
  N1: Arduino_Uno.A4/SDA, Lidar_LIte_V3.2, Screw_terminal.3, R1.Pin_1
  N2: Arduino_Uno.A5/SCL, Lidar_LIte_V3.3, Screw_terminal.4, R2.Pin_1
  GND: Arduino_Uno.GND, C1.+, Lidar_LIte_V3.1, Screw_terminal.2, J1.gnd, J2.gnd, JP1.1, JP2.1
  N3: Arduino_Uno.D9_PWM, J1.pulse, JP1.2
  N4: Arduino_Uno.D10_PWM/SS, J2.pulse, JP2.2
  VCC: Arduino_Uno.5V, C1.-, Lidar_LIte_V3.6, Screw_terminal.1, R1.Pin_0, R2.Pin_0, J1.vcc, J2.vcc, JP1.3, JP2.3

notes:
  Lidar dome distance scanner
